// Logisim project complete-4-bit-alu.circ as structural Verilog: 4 circuits, main circuit 4-bit ALU
// 1b ALU
module _1_bit_ALU (
  input  a_invert,
  input  b_invert,
  input  c_in,
  input  less,
  input  [1:0] operation,
  input  a,
  input  b,
  output result,
  output c_out
);

  wire adder_1_out, and_1_out, multiplexer_1_out, multiplexer_2_out, not_1_out, not_2_out, or_1_out;

  not not_1 (not_1_out, a);
  Multiplexer #(.enable("false")) multiplexer_1 (.in0(a), .in1(not_1_out), .out(multiplexer_1_out), .sel(a_invert));
  not not_2 (not_2_out, b);
  Multiplexer #(.enable("false")) multiplexer_2 (.in0(b), .in1(not_2_out), .out(multiplexer_2_out), .sel(b_invert));
  and and_1 (and_1_out, multiplexer_1_out, multiplexer_2_out);
  or or_1 (or_1_out, multiplexer_1_out, multiplexer_2_out);
  Adder #(.width(1)) adder_1 (
    .a(multiplexer_1_out), .b(multiplexer_2_out), .out(adder_1_out), .cin(c_in), .cout(c_out));
  Multiplexer #(.select(2), .enable("false")) multiplexer_3 (
    .in0(and_1_out), .in1(or_1_out), .in2(adder_1_out), .in3(less), .out(result), .sel(operation));
endmodule

// 4b ALU
module _4_bit_ALU (
  input  a_invert,
  input  b_invert,
  input  c_in,
  input  [1:0] operation,
  input  [3:0] a,
  input  [3:0] b,
  output [3:0] result,
  output overflow,
  output c_out
);

  wire msb_alu_1_c_in_prev, msb_alu_1_set, multiplexer_1_out, n1_bit_alu_1_c_out, n1_bit_alu_2_c_out,
       n1_bit_alu_3_c_out, not_1_out;

  _1_bit_ALU u_1_bit_alu_1 (
    .a(a[0]), .b(b[0]), .result(result[0]), .a_invert(a_invert), .b_invert(b_invert), .c_in(c_in),
    .operation(operation), .c_out(n1_bit_alu_1_c_out), .less(multiplexer_1_out));
  _1_bit_ALU u_1_bit_alu_2 (
    .a(a[1]), .b(b[1]), .result(result[1]), .a_invert(a_invert), .b_invert(b_invert),
    .c_in(n1_bit_alu_1_c_out), .operation(operation), .c_out(n1_bit_alu_2_c_out), .less(1'b0));
  _1_bit_ALU u_1_bit_alu_3 (
    .a(a[2]), .b(b[2]), .result(result[2]), .a_invert(a_invert), .b_invert(b_invert),
    .c_in(n1_bit_alu_2_c_out), .operation(operation), .c_out(n1_bit_alu_3_c_out), .less(1'b0));
  MSB_ALU msb_alu_1 (
    .a(a[3]), .b(b[3]), .result(result[3]), .set(msb_alu_1_set), .a_invert(a_invert), .b_invert(b_invert),
    .c_in(n1_bit_alu_3_c_out), .less(1'b0), .operation(operation), .c_out(c_out),
    .c_in_prev(msb_alu_1_c_in_prev));
  overflow_detector overflow_detector_1 (.c_out(c_out), .c_in(msb_alu_1_c_in_prev), .Overflow(overflow));
  Multiplexer #(.enable("false")) multiplexer_1 (
    .in0(msb_alu_1_set), .in1(not_1_out), .out(multiplexer_1_out), .sel(overflow));
  not not_1 (not_1_out, msb_alu_1_set);
endmodule

// MSB
module MSB_ALU (
  input  a_invert,
  input  b_invert,
  input  c_in,
  input  less,
  input  [1:0] operation,
  input  a,
  input  b,
  output result,
  output set,
  output c_out,
  output c_in_prev
);

  wire and_1_out, multiplexer_1_out, multiplexer_2_out, not_1_out, not_2_out, or_1_out;

  not not_1 (not_1_out, a);
  Multiplexer #(.enable("false")) multiplexer_1 (.in0(a), .in1(not_1_out), .out(multiplexer_1_out), .sel(a_invert));
  not not_2 (not_2_out, b);
  Multiplexer #(.enable("false")) multiplexer_2 (.in0(b), .in1(not_2_out), .out(multiplexer_2_out), .sel(b_invert));
  and and_1 (and_1_out, multiplexer_1_out, multiplexer_2_out);
  or or_1 (or_1_out, multiplexer_1_out, multiplexer_2_out);
  Adder #(.width(1)) adder_1 (.a(multiplexer_1_out), .b(multiplexer_2_out), .out(set), .cin(c_in), .cout(c_out));
  Multiplexer #(.select(2), .enable("false")) multiplexer_3 (
    .in0(and_1_out), .in1(or_1_out), .in2(set), .in3(less), .out(result), .sel(operation));

  assign c_in_prev = c_in;
endmodule

// OF
module overflow_detector (
  input  c_out,
  input  c_in,
  output Overflow
);

  xor xor_1 (Overflow, c_out, c_in);
endmodule
